# Fritzing sketch conexiones_breadboard (saved by Fritzing 0.9.3b)
breadboards: 1

parts:
  Part1 = Arduino Nano (Rev3.0)  # not connected
  Part2 = Bluetooth HC-06
  J1 = Basic Servo

nets:
  GND: Part2.GND, J1.gnd
  VCC: Part2.VCC, J1.vcc
